# Fritzing sketch diagram (saved by Fritzing 0.9.6b)
breadboards: 1

parts:
  Mod1 = Raspberry Pi Pico
  Part1 = Adafruit PDM Mic [part_number="Adafruit #3492"]
  Part4 = Adafruit 2.0 inch 240x320 IPS TFT [part_number="Adafruit #4311"]

nets:
  N1: Mod1.pin_3, Mod1.pin_8, Mod1.pin_13, Mod1.pin_18, Mod1.pin_23, Mod1.pin_28, Mod1.pin_33, Mod1.pin_38
  N2: Mod1.pin_4, Part1.DATA
  N3: Mod1.pin_5, Part1.CLK
  N4: Mod1.pin_22, Part4.LCDCS_5V
  N5: Mod1.pin_24, Part4.SCLK_5V
  N6: Mod1.pin_25, Part4.MOSI_5V
  N7: Mod1.pin_26, Part4.DC_5V
  N8: Mod1.pin_27, Part4.RESET_5V
  VDD: Mod1.pin_36, Part1.VDD, Part4.VIN
  GND: Part1.GND, Part1.SELECT, Part4.GND

custom parts:
  Raspberry Pi Pico: Raspberry Pi Pico. Based around the RP2040 microcontroller the Pico is a low cost microcontroller device bringing Raspberry Pi quality, cost, and easy of use to the microcontroller space. Jan 2021, Split part in to two versions: tht (this one) and SMD. This one will drill holes for a .1 in header in pcb to allow plugging in the module as well as providing pads to solder the module to the top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
  Adafruit PDM Mic: An exotic new microphone has arrived in the Adafruit shop, a PDM MEMS Microphone! PDM is the 'third' kind of microphone you can integrate with electronics, apart from analog or I2S. These microphones are very commonly used in products, but are rarely seen in maker projects. Still, they have some benefits so we thought we'd offer a breakout for the shop. The first thing to note is that this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
  Adafruit 2.0 inch 240x320 IPS TFT: This gorgeous IPS display breakout is the best way to add a small, colorful and bright display to any project, with excellent visibility from any angle. Since the display uses 4-wire SPI to communicate and has its own pixel-addressable frame buffer, it can be used with every kind of microcontroller. Even a very small one with low memory and few pins available! The 2.0" display has 320x240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
